// Digital circuit 4-Bit Full Adder.dig as structural Verilog
module _4_Bit_Full_Adder (
  input  [3:0] A,
  input  [3:0] B,
  input  K,
  output C_out,
  output [3:0] Sum
);

  wire _1_bit_full_adder_1_p5, _1_bit_full_adder_2_p5, _1_bit_full_adder_3_p5;

  // _1_Bit_Full_Adder _1_bit_full_adder_1: pin names not known; wires that end beside it: A[0], B[0], K, Sum[0], _1_bit_full_adder_1_p5
  // _1_Bit_Full_Adder _1_bit_full_adder_2: pin names not known; wires that end beside it: A[1], B[1], _1_bit_full_adder_1_p5, Sum[1], _1_bit_full_adder_2_p5
  // _1_Bit_Full_Adder _1_bit_full_adder_3: pin names not known; wires that end beside it: A[2], B[2], _1_bit_full_adder_2_p5, Sum[2], _1_bit_full_adder_3_p5
  // _1_Bit_Full_Adder _1_bit_full_adder_4: pin names not known; wires that end beside it: A[3], B[3], _1_bit_full_adder_3_p5, Sum[3], C_out
endmodule
