// Digital circuit 4BitAdder.dig as structural Verilog
module _4BitAdder (
  input  [3:0] A,
  input  [3:0] B,
  input  K,
  output C_out,
  output [3:0] Sum
);

  wire _1bitadder_1_cout, _1bitadder_2_cout, _1bitadder_3_cout;

  _1bitadder _1bitadder_1 (.A(A[0]), .B(B[0]), .Cin(K), .Sum(Sum[0]), .Cout(_1bitadder_1_cout));
  _1bitadder _1bitadder_2 (.A(A[1]), .B(B[1]), .Cin(_1bitadder_1_cout), .Sum(Sum[1]), .Cout(_1bitadder_2_cout));
  _1bitadder _1bitadder_3 (.A(A[2]), .B(B[2]), .Cin(_1bitadder_2_cout), .Sum(Sum[2]), .Cout(_1bitadder_3_cout));
  _1bitadder _1bitadder_4 (.A(A[3]), .B(B[3]), .Cin(_1bitadder_3_cout), .Sum(Sum[3]), .Cout(C_out));
endmodule
