// Digital circuit 5 step.dig as structural Verilog
module _5_step (
  input  clk,
  output [4:0] States,
  output IF1,
  output IF2,
  output WB,
  output Inc
);

  wire IF1_q;

  D_FF #(.Default(1)) u_IF1 (.D(IF1), .C(clk), .Q(IF1_q));  // open: nQ
  D_FF u_IF2 (.D(IF1_q), .C(clk), .Q(IF2));  // open: nQ
  D_FF Decode (.D(IF2), .C(clk), .Q(States[2]));  // open: nQ
  or or_1 (Inc, IF1, IF1);
  D_FF Execute (.D(States[2]), .C(clk), .Q(States[3]));  // open: nQ
  D_FF Write_Back (.D(States[3]), .C(clk), .Q(IF1));  // open: nQ

  assign {States[4], States[1:0]} = {IF1, IF2, IF1};
  assign WB = IF1;

  // Notes on the sheet:
  //   IF1: Instruction Fetch 1
endmodule
