// Digital circuit ALUFINAL.dig as structural Verilog
module ALUFINAL (
  input  [3:0] A,
  input  [3:0] B,
  input  [2:0] S_1_S_0_C_in,
  output [3:0] D,
  output C_out
);

  wire [3:0] multiplexer_1_out, not_1_out, not_2_out;

  assign not_1_out = ~B;  // Not not_1, 4 bits wide
  assign not_2_out = ~4'b0000;  // Not not_2, 4 bits wide
  Multiplexer #(.Selector_Bits(2), .Bits(4)) multiplexer_1 (
    .sel(S_1_S_0_C_in[2:1]), .in_0(B), .in_1(not_1_out), .in_2(4'b0000), .in_3(not_2_out),
    .out(multiplexer_1_out));
  Add _4_bit_adder (.a(A[0]), .b(S_1_S_0_C_in[0]), .c_i(multiplexer_1_out[0]), .s(C_out), .c_o(D[0]));
  // Pins of 1 and 4 bits meet at A
  // Pins of 1 and 4 bits meet at multiplexer_1_out
  // Pins of 1 and 4 bits meet at D
endmodule
