// Digital circuit DRAM.dig as structural Verilog
module DRAM (
  input  [3:0] Address_bits,
  input  Clk,
  input  [1:0] Control_bits,
  input  [3:0] Data_input,
  output [3:0] Output
);

  wire and_1_out, and_2_out, and_3_out, and_4_out, and_5_out, and_6_out, and_7_out, and_8_out, and_9_out,
       and_10_out, and_11_out, and_12_out, and_13_out, and_14_out, and_15_out, and_16_out, decoder_1_out_0,
       decoder_1_out_1, decoder_1_out_2, decoder_1_out_3, decoder_1_out_4, decoder_1_out_5, decoder_1_out_6,
       decoder_1_out_7, decoder_1_out_8, decoder_1_out_9, decoder_1_out_10, decoder_1_out_11,
       decoder_1_out_12, decoder_1_out_13, decoder_1_out_14, decoder_1_out_15;
  wire [3:0] Row_0_out, Row_1_out, Row_2_out, Row_3_out, Row_4_out, Row_5_out, Row_6_out, Row_7_out,
       Row_8_out, Row_9_out, Row_10_out, Row_11_out, Row_12_out, Row_13_out, Row_14_out, Row_15_out;

  Decoder #(.Selector_Bits(4)) decoder_1 (
    .sel(Address_bits), .out_0(decoder_1_out_0), .out_1(decoder_1_out_1), .out_2(decoder_1_out_2),
    .out_3(decoder_1_out_3), .out_4(decoder_1_out_4), .out_5(decoder_1_out_5), .out_6(decoder_1_out_6),
    .out_7(decoder_1_out_7), .out_8(decoder_1_out_8), .out_9(decoder_1_out_9), .out_10(decoder_1_out_10),
    .out_11(decoder_1_out_11), .out_12(decoder_1_out_12), .out_13(decoder_1_out_13),
    .out_14(decoder_1_out_14), .out_15(decoder_1_out_15));
  and and_1 (and_1_out, decoder_1_out_0, Clk);
  and and_2 (and_2_out, decoder_1_out_4, Clk);
  and and_3 (and_3_out, decoder_1_out_8, Clk);
  and and_4 (and_4_out, decoder_1_out_12, Clk);
  GPR Row_0 (.CSLI(Control_bits), .In(Data_input), .clk(and_1_out), .Out(Row_0_out));
  GPR Row_4 (.CSLI(Control_bits), .In(Data_input), .clk(and_2_out), .Out(Row_4_out));
  GPR Row_8 (.CSLI(Control_bits), .In(Data_input), .clk(and_3_out), .Out(Row_8_out));
  GPR Row_12 (.CSLI(Control_bits), .In(Data_input), .clk(and_4_out), .Out(Row_12_out));
  and and_5 (and_5_out, decoder_1_out_1, Clk);
  and and_6 (and_6_out, decoder_1_out_5, Clk);
  and and_7 (and_7_out, decoder_1_out_9, Clk);
  and and_8 (and_8_out, decoder_1_out_13, Clk);
  GPR Row_1 (.CSLI(Control_bits), .In(Data_input), .clk(and_5_out), .Out(Row_1_out));
  GPR Row_5 (.CSLI(Control_bits), .In(Data_input), .clk(and_6_out), .Out(Row_5_out));
  GPR Row_9 (.CSLI(Control_bits), .In(Data_input), .clk(and_7_out), .Out(Row_9_out));
  GPR Row_13 (.CSLI(Control_bits), .In(Data_input), .clk(and_8_out), .Out(Row_13_out));
  and and_9 (and_9_out, decoder_1_out_2, Clk);
  and and_10 (and_10_out, decoder_1_out_6, Clk);
  and and_11 (and_11_out, decoder_1_out_10, Clk);
  and and_12 (and_12_out, decoder_1_out_14, Clk);
  GPR Row_2 (.CSLI(Control_bits), .In(Data_input), .clk(and_9_out), .Out(Row_2_out));
  GPR Row_6 (.CSLI(Control_bits), .In(Data_input), .clk(and_10_out), .Out(Row_6_out));
  GPR Row_10 (.CSLI(Control_bits), .In(Data_input), .clk(and_11_out), .Out(Row_10_out));
  GPR Row_14 (.CSLI(Control_bits), .In(Data_input), .clk(and_12_out), .Out(Row_14_out));
  and and_13 (and_13_out, decoder_1_out_3, Clk);
  and and_14 (and_14_out, decoder_1_out_7, Clk);
  and and_15 (and_15_out, decoder_1_out_11, Clk);
  and and_16 (and_16_out, decoder_1_out_15, Clk);
  GPR Row_3 (.CSLI(Control_bits), .In(Data_input), .clk(and_13_out), .Out(Row_3_out));
  GPR Row_7 (.CSLI(Control_bits), .In(Data_input), .clk(and_14_out), .Out(Row_7_out));
  GPR Row_11 (.CSLI(Control_bits), .In(Data_input), .clk(and_15_out), .Out(Row_11_out));
  GPR Row_15 (.CSLI(Control_bits), .In(Data_input), .clk(and_16_out), .Out(Row_15_out));
  Multiplexer #(.Selector_Bits(4), .Bits(4)) multiplexer_1 (
    .sel(Address_bits), .in_0(Row_0_out), .in_1(Row_1_out), .in_2(Row_2_out), .in_3(Row_3_out),
    .in_4(Row_4_out), .in_5(Row_5_out), .in_6(Row_6_out), .in_7(Row_7_out), .in_8(Row_8_out),
    .in_9(Row_12_out), .in_10(Row_9_out), .in_11(Row_13_out), .in_12(Row_10_out), .in_13(Row_14_out),
    .in_14(Row_11_out), .in_15(Row_15_out), .out(Output));
endmodule
