// Digital circuit GPR.dig as structural Verilog
module GPR (
  input  [1:0] CLSI,
  input  [3:0] In,
  input  clk,
  output [3:0] Out
);

  wire [3:0] multiplexer_1_out;

  Multiplexer #(.Selector_Bits(2), .Bits(4)) multiplexer_1 (
    .sel(CLSI), .in_0(4'b0000), .in_1(In), .in_2(Out), .in_3(4'b1111), .out(multiplexer_1_out));
  D_FF d_ff_1 (.D(multiplexer_1_out[3]), .C(clk), .Q(Out[3]));  // open: nQ
  D_FF d_ff_2 (.D(multiplexer_1_out[2]), .C(clk), .Q(Out[2]));  // open: nQ
  D_FF d_ff_3 (.D(multiplexer_1_out[1]), .C(clk), .Q(Out[1]));  // open: nQ
  D_FF d_ff_4 (.D(multiplexer_1_out[0]), .C(clk), .Q(Out[0]));  // open: nQ

  // Notes on the sheet:
  //   CLSI: 0 clear
  //   2 store input
  //   2 load
  //   3 Increment
  //   In: clear store load increment
endmodule
